# Fritzing sketch 粉墨 (saved by Fritzing 0.9.8b)
circuit board: 3cm x 7.5cm
breadboards: 1

parts:
  元件1 = Arduino Nano (Rev3.0)
  高压包1 = LEDs [package=led10mm]
  电磁阀1 = LEDs [package=led10mm]
  Q1 = NPN-Transistor [package="SOT-23 [SMD]"]
  R1 = Resistor [tolerance=±5% power=0.25 resistance=220 package=THT]
  灯带1 = LEDs [package=led10mm]

nets (from the pcb view):
  N1: 元件1.GND, 高压包1.C, 电磁阀1.C, R1.Pin_0
  N2: 元件1.VIN, Q1.0, 灯带1.A
  N3: 电磁阀1.A, Q1.1
  N4: R1.Pin_1, 灯带1.C
